// Logisim project fib.circ as structural Verilog: 1 circuit, main circuit main
module main (
  input  [2:0] in_1,
  output [3:0] out_2
);

  wire clock_1_out, comparator_1_eq, comparator_2_eq, comparator_2_lt, nor_1_out;
  wire [2:0] counter_1_q;
  wire [3:0] adder_1_out, register_1_q, register_2_q;

  Counter #(.width(3), .max('h7), .ongoal("stay")) counter_1 (
    .Q(counter_1_q), .clk(clock_1_out));  // open: load, D, count, carry, clr
  Comparator #(.width(3), .mode("unsigned")) comparator_1 (
    .a(3'b000), .b(counter_1_q), .eq(comparator_1_eq));  // open: gt, lt
  Comparator #(.width(3), .mode("unsigned")) comparator_2 (
    .a(in_1), .b(counter_1_q), .eq(comparator_2_eq), .lt(comparator_2_lt));  // open: gt
  Clock clock_1 (.out(clock_1_out));
  nor nor_1 (nor_1_out, comparator_2_eq, comparator_2_lt);
  Register #(.width(4)) register_1 (.D(adder_1_out), .en(nor_1_out), .Q(register_1_q), .clk(clock_1_out));  // open: clr
  Register #(.width(4)) register_2 (
    .D(register_1_q), .en(nor_1_out), .Q(register_2_q), .clk(clock_1_out));  // open: clr
  Multiplexer #(.width(4), .enable("false")) multiplexer_1 (
    .in0(register_1_q), .in1(4'b0000), .out(out_2), .sel(nor_1_out));
  Adder #(.width(4)) adder_1 (
    .a(register_1_q), .b(register_2_q), .out(adder_1_out), .cin(comparator_1_eq));  // open: cout
endmodule
