// Logisim project fib_2.circ as structural Verilog: 7 circuits, main circuit main
module main (
  input  [31:0] N,
  output [31:0] out_2
);

  wire input_1__0_1, input_1_init, input_1_valid;
  wire [31:0] initmatrix_1_m_11, initmatrix_1_m_12, initmatrix_1_m_21, initmatrix_1_m_22,
       matrixstore_1_m2_11, matrixstore_1_m2_12, matrixstore_1_m2_21, matrixstore_1_m2_22, squre_0_1_1_m2_11,
       squre_0_1_1_m2_12, squre_0_1_1_m2_21, squre_0_1_1_m2_22;

  Input input_1 (.N(N), ._0_1(input_1__0_1), .Valid(input_1_valid), .Init(input_1_init));
  InitMatrix initmatrix_1 (
    .M1_11(matrixstore_1_m2_11), .M1_12(matrixstore_1_m2_12), .M1_21(matrixstore_1_m2_21),
    .M1_22(matrixstore_1_m2_22), .M_11(initmatrix_1_m_11), .M_12(initmatrix_1_m_12),
    .M_21(initmatrix_1_m_21), .M_22(initmatrix_1_m_22), .Init(input_1_init));
  Squre_0_1 squre_0_1_1 (
    .M1_11(initmatrix_1_m_11), .M1_12(initmatrix_1_m_12), .M1_21(initmatrix_1_m_21),
    .M1_22(initmatrix_1_m_22), ._0_1(input_1__0_1), .M2_11(squre_0_1_1_m2_11), .M2_12(squre_0_1_1_m2_12),
    .M2_21(squre_0_1_1_m2_21), .M2_22(squre_0_1_1_m2_22));
  MatrixStore matrixstore_1 (
    .M1_11(squre_0_1_1_m2_11), .M2_11(matrixstore_1_m2_11), .M1_12(squre_0_1_1_m2_12),
    .M2_12(matrixstore_1_m2_12), .M1_21(squre_0_1_1_m2_21), .M2_21(matrixstore_1_m2_21),
    .M1_22(squre_0_1_1_m2_22), .M2_22(matrixstore_1_m2_22), .Enable(input_1_valid));
  Output output_1 (.N(N), .Calc(initmatrix_1_m_12), .Output(out_2));
endmodule

module MartixMultiplier (
  input  [31:0] M1_11,
  input  [31:0] M2_11,
  input  [31:0] M1_12,
  input  [31:0] M2_12,
  input  [31:0] M1_21,
  input  [31:0] M2_21,
  input  [31:0] M1_22,
  input  [31:0] M2_22,
  output [31:0] M_11,
  output [31:0] M_12,
  output [31:0] M_21,
  output [31:0] M_22
);

  wire [31:0] multiplier_1_out, multiplier_2_out, multiplier_3_out, multiplier_4_out, multiplier_5_out,
       multiplier_6_out, multiplier_7_out, multiplier_8_out;

  Multiplier #(.width(32)) multiplier_1 (.a(M1_11), .b(M2_11), .out(multiplier_1_out));  // open: cin, cout
  Multiplier #(.width(32)) multiplier_2 (.a(M1_12), .b(M2_21), .out(multiplier_2_out));  // open: cin, cout
  Multiplier #(.width(32)) multiplier_3 (.a(M1_11), .b(M2_12), .out(multiplier_3_out));  // open: cin, cout
  Multiplier #(.width(32)) multiplier_4 (.a(M1_12), .b(M2_22), .out(multiplier_4_out));  // open: cin, cout
  Multiplier #(.width(32)) multiplier_5 (.a(M1_21), .b(M2_11), .out(multiplier_5_out));  // open: cin, cout
  Multiplier #(.width(32)) multiplier_6 (.a(M1_22), .b(M2_21), .out(multiplier_6_out));  // open: cin, cout
  Multiplier #(.width(32)) multiplier_7 (.a(M1_21), .b(M2_12), .out(multiplier_7_out));  // open: cin, cout
  Multiplier #(.width(32)) multiplier_8 (.a(M1_22), .b(M2_22), .out(multiplier_8_out));  // open: cin, cout
  Adder #(.width(32)) adder_1 (.a(multiplier_1_out), .b(multiplier_2_out), .out(M_11));  // open: cin, cout
  Adder #(.width(32)) adder_2 (.a(multiplier_3_out), .b(multiplier_4_out), .out(M_12));  // open: cin, cout
  Adder #(.width(32)) adder_3 (.a(multiplier_5_out), .b(multiplier_6_out), .out(M_21));  // open: cin, cout
  Adder #(.width(32)) adder_4 (.a(multiplier_7_out), .b(multiplier_8_out), .out(M_22));  // open: cin, cout
endmodule

module MatrixStore (
  input  [31:0] M1_11,
  input  [31:0] M1_12,
  input  Enable,
  input  [31:0] M1_21,
  input  [31:0] M1_22,
  output [31:0] M2_11,
  output [31:0] M2_12,
  output [31:0] M2_21,
  output [31:0] M2_22
);

  wire clock_1_out;

  Clock clock_1 (.out(clock_1_out));
  Register #(.width(32)) register_1 (.D(M1_11), .en(Enable), .Q(M2_11), .clk(clock_1_out));  // open: clr
  Register #(.width(32)) register_2 (.D(M1_12), .en(Enable), .Q(M2_12), .clk(clock_1_out));  // open: clr
  Register #(.width(32)) register_3 (.D(M1_21), .en(Enable), .Q(M2_21), .clk(clock_1_out));  // open: clr
  Register #(.width(32)) register_4 (.D(M1_22), .en(Enable), .Q(M2_22), .clk(clock_1_out));  // open: clr
endmodule

module Squre_0_1 (
  input  [31:0] M1_11,
  input  [31:0] M1_12,
  input  [31:0] M1_21,
  input  [31:0] M1_22,
  input  _0_1,
  output [31:0] M2_11,
  output [31:0] M2_12,
  output [31:0] M2_21,
  output [31:0] M2_22
);

  wire [31:0] martixmultiplier_1_m_11, martixmultiplier_1_m_12, martixmultiplier_1_m_21,
       martixmultiplier_1_m_22, multiplexer_1_out, multiplexer_2_out, multiplexer_3_out, multiplexer_4_out;

  MartixMultiplier martixmultiplier_1 (
    .M1_11(M1_11), .M2_11(M1_11), .M1_12(M1_12), .M2_12(M1_12), .M1_21(M1_21), .M2_21(M1_21), .M1_22(M1_22),
    .M2_22(M1_22), .M_11(martixmultiplier_1_m_11), .M_12(martixmultiplier_1_m_12),
    .M_21(martixmultiplier_1_m_21), .M_22(martixmultiplier_1_m_22));
  MartixMultiplier martixmultiplier_2 (
    .M1_11(martixmultiplier_1_m_11), .M2_11(multiplexer_1_out), .M1_12(martixmultiplier_1_m_12),
    .M2_12(multiplexer_2_out), .M1_21(martixmultiplier_1_m_21), .M2_21(multiplexer_3_out),
    .M1_22(martixmultiplier_1_m_22), .M2_22(multiplexer_4_out), .M_11(M2_11), .M_12(M2_12), .M_21(M2_21),
    .M_22(M2_22));
  Multiplexer #(.width(32), .enable("false")) multiplexer_1 (
    .in0(32'h1), .in1(32'h1), .out(multiplexer_1_out), .sel(_0_1));
  Multiplexer #(.width(32), .enable("false")) multiplexer_2 (
    .in0({32{1'b0}}), .in1(32'h1), .out(multiplexer_2_out), .sel(_0_1));
  Multiplexer #(.width(32), .enable("false")) multiplexer_3 (
    .in0({32{1'b0}}), .in1(32'h1), .out(multiplexer_3_out), .sel(_0_1));
  Multiplexer #(.width(32), .enable("false")) multiplexer_4 (
    .in0(32'h1), .in1({32{1'b0}}), .out(multiplexer_4_out), .sel(_0_1));
endmodule

module InitMatrix (
  input  [31:0] M1_11,
  input  [31:0] M1_12,
  input  [31:0] M1_21,
  input  [31:0] M1_22,
  input  Init,
  output [31:0] M_11,
  output [31:0] M_12,
  output [31:0] M_21,
  output [31:0] M_22
);

  Multiplexer #(.width(32), .enable("false")) multiplexer_1 (.in0(M1_11), .in1(32'h1), .out(M_11), .sel(Init));
  Multiplexer #(.width(32), .enable("false")) multiplexer_2 (.in0(M1_12), .in1(32'h1), .out(M_12), .sel(Init));
  Multiplexer #(.width(32), .enable("false")) multiplexer_3 (.in0(M1_21), .in1(32'h1), .out(M_21), .sel(Init));
  Multiplexer #(.width(32), .enable("false")) multiplexer_4 (.in0(M1_22), .in1({32{1'b0}}), .out(M_22), .sel(Init));
endmodule

module Input (
  input  [31:0] N,
  output _0_1,
  output Valid,
  output Init
);

  wire clock_1_out, comparator_1_eq, comparator_2_lt, not_1_out, or_1_out, register_2_q;
  wire [7:0] counter_2_q;
  wire [30:0] multiplexer_1_out;
  wire [31:0] counter_1_q, register_1_q, shifter_1_out;

  Counter #(.width(32), .max('hffffffff), .ongoal("stay")) counter_1 (
    .Q(counter_1_q), .clk(clock_1_out));  // open: load, D, count, carry, clr
  Clock clock_1 (.out(clock_1_out));
  Multiplexer #(.width(32), .enable("false")) multiplexer_1 (
    .in0(register_1_q), .in1(N), .out({_0_1, multiplexer_1_out}), .sel(comparator_1_eq));
  Comparator #(.width(32), .mode("unsigned")) comparator_1 (
    .a(32'h1), .b(counter_1_q), .eq(comparator_1_eq));  // open: gt, lt
  Comparator #(.width(32), .mode("unsigned")) comparator_2 (
    .a(32'h20), .b(counter_1_q), .lt(comparator_2_lt));  // open: gt, eq
  Shifter #(.width(32)) shifter_1 (.in({_0_1, multiplexer_1_out}), .\dist (5'b00001), .out(shifter_1_out));
  Register #(.width(32)) register_1 (.D(shifter_1_out), .Q(register_1_q), .clk(clock_1_out));  // open: en, clr
  Register #(.width(1), .trigger("high")) register_2 (.D(_0_1), .Q(register_2_q), .clk(not_1_out));  // open: en, clr
  not not_1 (not_1_out, register_2_q);
  and and_1 (Valid, register_2_q, ~comparator_2_lt);  // AND_Gate
  Counter #(.ongoal("stay")) counter_2 (
    .count(or_1_out), .Q(counter_2_q), .clk(clock_1_out));  // open: load, D, carry, clr
  or or_1 (or_1_out, Init, _0_1);
  Comparator comparator_3 (.a(counter_2_q), .b(8'h1), .eq(Init));  // open: gt, lt
endmodule

module Output (
  input  [31:0] N,
  input  [31:0] Calc,
  output [31:0] Output
);

  wire clock_1_out, comparator_3_lt;
  wire [1:0] comparator_1_gt;
  wire [31:0] counter_1_q, multiplexer_1_out;

  Comparator #(.width(32), .mode("unsigned")) comparator_1 (
    .a(N), .b({32{1'b0}}), .gt(comparator_1_gt[0]));  // open: eq, lt
  Comparator #(.width(32), .mode("unsigned")) comparator_2 (.a(N), .b(32'h1), .gt(comparator_1_gt[1]));  // open: eq, lt
  Multiplexer #(.select(2), .width(32), .enable("false")) multiplexer_1 (
    .in0({32{1'b0}}), .in1(32'h1), .in3(Calc), .out(multiplexer_1_out), .sel(comparator_1_gt));  // open: in2
  Clock clock_1 (.out(clock_1_out));
  Comparator #(.width(32), .mode("unsigned")) comparator_3 (
    .a(32'h20), .b(counter_1_q), .lt(comparator_3_lt));  // open: gt, eq
  Counter #(.width(32), .max('hffffffff)) counter_1 (
    .Q(counter_1_q), .clk(clock_1_out));  // open: load, D, count, carry, clr
  Multiplexer #(.width(32), .enable("false")) multiplexer_2 (
    .in0({32{1'b0}}), .in1(multiplexer_1_out), .out(Output), .sel(comparator_3_lt));
endmodule
