// Logisim project mod5.circ as structural Verilog: 3 circuits, main circuit mod5
module mod5 (
  input  In,
  output s0,
  output s1,
  output s2,
  output s3,
  output s4
);

  wire clock_1_out;
  wire [4:0] register_1_q;

  trans trans_1 (
    .In(In), .S0(register_1_q[0]), .S1(register_1_q[1]), .S2(register_1_q[2]), .S3(register_1_q[3]),
    .S4(register_1_q[4]), .O0(s0), .O1(s1), .O2(s2), .O3(s3), .O4(s4));
  Register #(.width(5)) register_1 (.D({s4, s3, s2, s1, s0}), .Q(register_1_q), .clk(clock_1_out));  // open: en, clr
  Clock clock_1 (.out(clock_1_out));
endmodule

module trans (
  input  In,
  input  S0,
  input  S1,
  input  S2,
  input  S3,
  input  S4,
  output O0,
  output O1,
  output O2,
  output O3,
  output O4
);

  wire and_3_out, and_4_out, and_5_out, and_6_out, not_1_out, not_2_out, not_3_out, not_4_out, not_5_out,
       not_6_out, not_7_out, not_8_out, not_9_out, not_10_out, not_11_out, not_12_out, not_13_out,
       not_14_out, not_15_out, not_16_out, not_17_out, not_18_out, not_19_out, not_20_out, not_21_out;

  not not_1 (not_1_out, In);
  not not_2 (not_2_out, S0);
  not not_3 (not_3_out, S2);
  not not_4 (not_4_out, S3);
  not not_5 (not_5_out, S0);
  not not_6 (not_6_out, S2);
  not not_7 (not_7_out, S3);
  not not_8 (not_8_out, S0);
  not not_9 (not_9_out, S1);
  not not_10 (not_10_out, S4);
  not not_11 (not_11_out, S0);
  not not_12 (not_12_out, S1);
  not not_13 (not_13_out, S4);
  not not_14 (not_14_out, In);
  not not_15 (not_15_out, S0);
  not not_16 (not_16_out, S1);
  not not_17 (not_17_out, S4);
  not not_18 (not_18_out, In);
  not not_19 (not_19_out, S0);
  not not_20 (not_20_out, S1);
  not not_21 (not_21_out, S4);
  and and_1 (O1, not_1_out, not_2_out, not_3_out, not_4_out);
  and and_2 (O2, In, not_5_out, not_6_out, not_7_out);
  and and_3 (and_3_out, In, not_8_out, not_9_out, S3, not_10_out);
  and and_4 (and_4_out, In, not_11_out, not_12_out, S2, not_13_out);
  and and_5 (and_5_out, not_14_out, not_15_out, not_16_out, S3, not_17_out);
  and and_6 (and_6_out, not_18_out, not_19_out, not_20_out, S2, not_21_out);
  or or_1 (O3, and_3_out, and_4_out);
  or or_2 (O4, and_5_out, and_6_out);

  assign O0 = S0;
endmodule

module test (
  output out_1,
  output out_2,
  output out_3,
  output out_4,
  output out_5,
  output out_6
);

  wire clock_1_out, counter_1_carry;
  wire [4:0] counter_1_q;

  Clock clock_1 (.out(clock_1_out));
  Counter #(.width(5), .max('hf)) counter_1 (
    .Q(counter_1_q), .carry(counter_1_carry), .clk(clock_1_out));  // open: load, D, count, clr
  ROM #(.addrWidth(5), .dataWidth(1)) rom_1 (.addr(counter_1_q), .data(out_1));  // open: sel
  mod5 mod5_1 (.In(out_1), .s0(out_2), .s1(out_3), .s2(out_4), .s3(out_5), .s4(out_6));
  // also tied to GND on the sheet: counter_1_carry

  // Notes on the sheet:
  //   contents of rom_1 (hex, n*v repeats v):
  //   1 0 0 0 1 0 0 1 0 0 1 0 0 1
endmodule
