// Logisim project t2.circ as structural Verilog: 1 circuit, main circuit main
module main (
  input  [3:0] in_1
);

  wire [0:0] undriven;
  wire [3:0] demultiplexer_1_out0, demultiplexer_1_out1, or_1_out;

  Demultiplexer #(.width(4)) demultiplexer_1 (
    .out0(demultiplexer_1_out0), .out1(demultiplexer_1_out1), .in(in_1));  // open: sel, en
  assign or_1_out = {demultiplexer_1_out0[2:0], undriven[0]} | demultiplexer_1_out1;  // OR_Gate or_1, 4 bits wide
endmodule
