// Logisim project test.circ as structural Verilog: 1 circuit, main circuit main
module main (
  output out_1,
  output out_2,
  output out_3,
  output out_4,
  output out_5,
  output out_6
);

  wire clock_1_out, counter_1_carry;
  wire [4:0] counter_1_q;

  Clock clock_1 (.out(clock_1_out));
  Counter #(.width(5), .max('hf)) counter_1 (
    .Q(counter_1_q), .carry(counter_1_carry), .clk(clock_1_out));  // open: load, D, count, clr
  ROM #(.addrWidth(5), .dataWidth(1)) rom_1 (.addr(counter_1_q), .data(out_1));  // open: sel
  // also tied to GND on the sheet: counter_1_carry

  // Notes on the sheet:
  //   contents of rom_1 (hex, n*v repeats v):
  //   0 1 0 0 1 0 0 1 0 0 1 0 0 1
endmodule
